// Digital circuit Adolph the Multiplicative Dolphin.dig as structural Verilog
module Adolph_the_Multiplicative_Dolphin (
  input  [3:0] b,
  input  [3:0] a,
  output [7:0] out_3
);

  wire [3:0] add_1_s, multiplexer_1_out, multiplexer_2_out, multiplexer_3_out, multiplexer_4_out;
  wire [3:1] add_2_s, add_3_s;
  wire [3:3] add_2_c_o, add_3_c_o, pulldown_1_out;

  PullDown pulldown_1 (.out(pulldown_1_out[3]));
  Multiplexer #(.Bits(4)) multiplexer_1 (.sel(b[0]), .in_0({4{pulldown_1_out[3]}}), .in_1(a), .out(multiplexer_1_out));
  Multiplexer #(.Bits(4)) multiplexer_2 (.sel(b[1]), .in_0({4{pulldown_1_out[3]}}), .in_1(a), .out(multiplexer_2_out));
  Multiplexer #(.Bits(4)) multiplexer_3 (.sel(b[2]), .in_0({4{pulldown_1_out[3]}}), .in_1(a), .out(multiplexer_3_out));
  Add #(.Bits(4)) add_1 (
    .a(multiplexer_1_out), .b({4{pulldown_1_out[3]}}), .c_i(pulldown_1_out[3]), .s({add_1_s[2:0], out_3[0]}),
    .c_o(add_1_s[3]));
  Multiplexer #(.Bits(4)) multiplexer_4 (.sel(b[3]), .in_0({4{pulldown_1_out[3]}}), .in_1(a), .out(multiplexer_4_out));
  Add #(.Bits(4)) add_2 (
    .a(multiplexer_2_out), .b(add_1_s), .c_i(pulldown_1_out[3]), .s({add_2_s, out_3[1]}), .c_o(add_2_c_o[3]));
  Add #(.Bits(4)) add_3 (
    .a(multiplexer_3_out), .b({add_2_c_o[3], add_2_s}), .c_i(pulldown_1_out[3]), .s({add_3_s, out_3[2]}),
    .c_o(add_3_c_o[3]));
  Add #(.Bits(4)) add_4 (
    .a(multiplexer_4_out), .b({add_3_c_o[3], add_3_s}), .c_i(pulldown_1_out[3]), .s(out_3[6:3]),
    .c_o(out_3[7]));
endmodule
