// Digital circuit Associative Memory.dig as structural Verilog
module Associative_Memory (
  input  Store,
  input  [3:0] Key,
  input  [2:0] Store_Address,
  input  [7:0] Value_In,
  input  clk,
  output [7:0] Value_Out,
  output [2:0] Found_At,
  output Found
);

  wire comparator_1_eq, comparator_2_eq, comparator_3_eq, comparator_4_eq, comparator_5_eq, comparator_6_eq,
       comparator_7_eq, comparator_8_eq, demultiplexer_1_out_0, demultiplexer_1_out_1, demultiplexer_1_out_2,
       demultiplexer_1_out_3, demultiplexer_1_out_4, demultiplexer_1_out_5, demultiplexer_1_out_6,
       demultiplexer_1_out_7, demultiplexer_2_out_0, demultiplexer_2_out_1, demultiplexer_2_out_2,
       demultiplexer_2_out_3, demultiplexer_2_out_4, demultiplexer_2_out_5, demultiplexer_2_out_6,
       demultiplexer_2_out_7;
  wire [3:0] register_1_q, register_2_q, register_3_q, register_4_q, register_5_q, register_6_q,
       register_7_q, register_8_q;
  wire [7:0] register_9_q, register_10_q, register_11_q, register_12_q, register_13_q, register_14_q,
       register_15_q, register_16_q;

  Demultiplexer #(.Selector_Bits(3)) demultiplexer_1 (
    .sel(Store_Address), .in(Store), .out_0(demultiplexer_1_out_0), .out_1(demultiplexer_1_out_1),
    .out_2(demultiplexer_1_out_2), .out_3(demultiplexer_1_out_3), .out_4(demultiplexer_1_out_4),
    .out_5(demultiplexer_1_out_5), .out_6(demultiplexer_1_out_6), .out_7(demultiplexer_1_out_7));
  Register #(.Bits(4)) register_1 (.D(Key), .C(clk), .en(demultiplexer_1_out_0), .Q(register_1_q));
  Register #(.Bits(4)) register_2 (.D(Key), .C(clk), .en(demultiplexer_1_out_1), .Q(register_2_q));
  Register #(.Bits(4)) register_3 (.D(Key), .C(clk), .en(demultiplexer_1_out_2), .Q(register_3_q));
  Register #(.Bits(4)) register_4 (.D(Key), .C(clk), .en(demultiplexer_1_out_3), .Q(register_4_q));
  Register #(.Bits(4)) register_5 (.D(Key), .C(clk), .en(demultiplexer_1_out_4), .Q(register_5_q));
  Register #(.Bits(4)) register_6 (.D(Key), .C(clk), .en(demultiplexer_1_out_5), .Q(register_6_q));
  Register #(.Bits(4)) register_7 (.D(Key), .C(clk), .en(demultiplexer_1_out_6), .Q(register_7_q));
  Register #(.Bits(4)) register_8 (.D(Key), .C(clk), .en(demultiplexer_1_out_7), .Q(register_8_q));
  Comparator #(.Bits(4)) comparator_1 (.a(Key), .b(register_1_q), .eq(comparator_1_eq));  // open: gt, lt
  Comparator #(.Bits(4)) comparator_2 (.a(Key), .b(register_2_q), .eq(comparator_2_eq));  // open: gt, lt
  Comparator #(.Bits(4)) comparator_3 (.a(Key), .b(register_3_q), .eq(comparator_3_eq));  // open: gt, lt
  Comparator #(.Bits(4)) comparator_4 (.a(Key), .b(register_4_q), .eq(comparator_4_eq));  // open: gt, lt
  Comparator #(.Bits(4)) comparator_5 (.a(Key), .b(register_5_q), .eq(comparator_5_eq));  // open: gt, lt
  Comparator #(.Bits(4)) comparator_6 (.a(Key), .b(register_6_q), .eq(comparator_6_eq));  // open: gt, lt
  Comparator #(.Bits(4)) comparator_7 (.a(Key), .b(register_7_q), .eq(comparator_7_eq));  // open: gt, lt
  Comparator #(.Bits(4)) comparator_8 (.a(Key), .b(register_8_q), .eq(comparator_8_eq));  // open: gt, lt
  PriorityEncoder #(.Selector_Bits(3)) priorityencoder_1 (
    .in0(comparator_1_eq), .in1(comparator_2_eq), .in2(comparator_3_eq), .in3(comparator_4_eq),
    .in4(comparator_5_eq), .in5(comparator_6_eq), .in6(comparator_7_eq), .in7(comparator_8_eq),
    .num(Found_At), .any(Found));
  Demultiplexer #(.Selector_Bits(3)) demultiplexer_2 (
    .sel(Store_Address), .in(Store), .out_0(demultiplexer_2_out_0), .out_1(demultiplexer_2_out_1),
    .out_2(demultiplexer_2_out_2), .out_3(demultiplexer_2_out_3), .out_4(demultiplexer_2_out_4),
    .out_5(demultiplexer_2_out_5), .out_6(demultiplexer_2_out_6), .out_7(demultiplexer_2_out_7));
  Register #(.Bits(8)) register_9 (.D(Value_In), .C(clk), .en(demultiplexer_2_out_0), .Q(register_9_q));
  Register #(.Bits(8)) register_10 (.D(Value_In), .C(clk), .en(demultiplexer_2_out_1), .Q(register_10_q));
  Register #(.Bits(8)) register_11 (.D(Value_In), .C(clk), .en(demultiplexer_2_out_2), .Q(register_11_q));
  Register #(.Bits(8)) register_12 (.D(Value_In), .C(clk), .en(demultiplexer_2_out_3), .Q(register_12_q));
  Register #(.Bits(8)) register_13 (.D(Value_In), .C(clk), .en(demultiplexer_2_out_4), .Q(register_13_q));
  Register #(.Bits(8)) register_14 (.D(Value_In), .C(clk), .en(demultiplexer_2_out_5), .Q(register_14_q));
  Register #(.Bits(8)) register_15 (.D(Value_In), .C(clk), .en(demultiplexer_2_out_6), .Q(register_15_q));
  Register #(.Bits(8)) register_16 (.D(Value_In), .C(clk), .en(demultiplexer_2_out_7), .Q(register_16_q));
  Multiplexer #(.Selector_Bits(3), .Bits(8)) multiplexer_1 (
    .sel(Found_At), .in_0(register_9_q), .in_1(register_10_q), .in_2(register_11_q), .in_3(register_12_q),
    .in_4(register_13_q), .in_5(register_14_q), .in_6(register_15_q), .in_7(register_16_q), .out(Value_Out));
endmodule
